// Logisim project Lab5.circ as structural Verilog
module FullAdder (
  input  a,
  input  b,
  input  c_in,
  output sum,
  output c_out
);

  wire and_1_out, and_2_out, xor_1_out;

  xor xor_1 (xor_1_out, a, b);
  and and_1 (and_1_out, xor_1_out, c_in);
  and and_2 (and_2_out, b, a);
  xor xor_2 (sum, xor_1_out, c_in);
  or or_1 (c_out, and_1_out, and_2_out);
endmodule

module FullAdder4Bit (
  input  [3:0] a,
  input  [3:0] b,
  input  in_3,
  output [3:0] sum,
  output out_5
);

  wire fulladder_1_c_out, fulladder_2_c_out, fulladder_3_c_out;

  FullAdder fulladder_1 (.a(a[0]), .b(b[0]), .c_in(in_3), .c_out(fulladder_1_c_out), .sum(sum[0]));
  FullAdder fulladder_2 (.a(a[1]), .b(b[1]), .c_in(fulladder_1_c_out), .c_out(fulladder_2_c_out), .sum(sum[1]));
  FullAdder fulladder_3 (.a(a[2]), .b(b[2]), .c_in(fulladder_2_c_out), .c_out(fulladder_3_c_out), .sum(sum[2]));
  FullAdder fulladder_4 (.a(a[3]), .b(b[3]), .c_in(fulladder_3_c_out), .c_out(out_5), .sum(sum[3]));

  // Other names for the same wires on the sheet: c_in = in_3; c_out = out_5; s0 = sum[0]; s1 = sum[1]; s2 = sum[2];
  //   s3 = sum[3]

  // Notes on the sheet:
  //   Inputs
  //   Outputs
endmodule
