// Logisim project mem.circ as structural Verilog: 4 circuits, main circuit main
module main (
  input  [7:0] inp,
  input  clk,
  input  set,
  input  [1:0] in_4
);

  wire and_1_out, and_2_out, and_3_out, and_4_out, decoder_1_out0, decoder_1_out1, decoder_1_out2,
       decoder_1_out3, register_8_bit_1_p4;

  Decoder #(.select(2)) decoder_1 (
    .out0(decoder_1_out0), .out1(decoder_1_out1), .out2(decoder_1_out2), .out3(decoder_1_out3), .sel(in_4));  // open: en
  and and_1 (and_1_out, set, decoder_1_out0);
  and and_2 (and_2_out, set, decoder_1_out1);
  and and_3 (and_3_out, set, decoder_1_out2);
  and and_4 (and_4_out, set, decoder_1_out3);
  // register_8_bit register_8_bit_1: pin names not known; wires that end beside it: clk, and_1_out, inp, register_8_bit_1_p4
  RAM ram_1 ();  // open: addr, we, oe, clk, din, dout
endmodule

module register_1_bit (
  input  e,
  input  D,
  input  clk,
  input  WE,
  output Q
);

  wire and_1_out, and_2_out, not_1_out, s_r_ff_1_q;

  and and_1 (and_1_out, D, WE);
  not not_1 (not_1_out, and_1_out);
  and and_2 (and_2_out, not_1_out, WE);
  S_R_Flip_Flop s_r_ff_1 (.S(and_1_out), .R(and_2_out), .clk(clk), .Q(s_r_ff_1_q));  // open: reset, Qn, preset
  and and_3 (Q, e, s_r_ff_1_q);
endmodule

module register_4_bit (
  input  clk,
  input  E,
  input  WE,
  input  [3:0] D,
  output [3:0] Q
);

  register_1_bit register_1_bit_1 (.D(D[0]), .WE(WE), .clk(clk), .e(E), .Q(Q[0]));
  register_1_bit register_1_bit_2 (.D(D[1]), .WE(WE), .clk(clk), .e(E), .Q(Q[1]));
  register_1_bit register_1_bit_3 (.D(D[2]), .WE(WE), .clk(clk), .e(E), .Q(Q[2]));
  register_1_bit register_1_bit_4 (.D(D[3]), .WE(WE), .clk(clk), .e(E), .Q(Q[3]));
endmodule

module register_8_bit (
  input  clk,
  input  WE,
  input  [7:0] D,
  input  E,
  output [7:0] Q
);

  register_4_bit register_4_bit_1 (.WE(WE), .E(E), .D(D[3:0]), .Q(Q[3:0]));  // open: clk
  register_4_bit register_4_bit_2 (.clk(clk), .WE(WE), .E(E), .D(D[7:4]), .Q(Q[7:4]));
endmodule
